# Fritzing sketch final project (saved by Fritzing 0.9.3b)
breadboards: 1

parts:
  ESP8267 = NodeMCU V1.0
  Componente2 = RFID-RC522-v2
  Part1 = LCD1602-I2C
  J1 = Piezo Speaker

nets:
  N1: ESP8267.D1, Part1.SCL
  N2: ESP8267.D2, Part1.SDA
  N3: ESP8267.D3, Componente2.RST
  N4: ESP8267.D4, Componente2.SDA
  3V3: ESP8267.3V3, Componente2.3.3V
  GND: ESP8267.GND, Componente2.GND, Part1.GND, J1.pin1
  N5: ESP8267.D5, Componente2.SCK
  N6: ESP8267.D6, Componente2.MISO
  N7: ESP8267.D7, Componente2.MOSI
  N8: ESP8267.D8, J1.pin2
  VIN: ESP8267.Vin, Part1.VCC

custom parts:
  NodeMCU V1.0: ESP8266 based NodeMCU
  RFID-RC522-v2: A simple China made RFID-RC522 Reader; do check the pin labels, as this is a MFRC522 based clone.
  LCD1602-I2C: A standard character display, usually with 2x16 characters. Comes in many colors with LCM1602 IIC attached.
